# Fritzing sketch Fridge Fritzing shcematic (saved by Fritzing 0.9.3b)
breadboards: 1

parts:
  WeMos_D1_Mini1 = WeMos D1 Mini
  WeMos_D1_Mini2 = WeMos D1 Mini
  DS1 = DS18B20 1-Wire Temperature Sensor [part_number=DS18B20]
  Part1 = ws2812b [package="smd 2812b"]
  U1 = RELAY-SOLIDSTATE [package=relay-s108t02]
  V1 = AC Power [voltage=5 frequency=60]
  HLK-PM1 = HLK-PM01
  U2 = Vibration Motor- ROB-08449 [package=vibe-motor-10mm]
  S1 = Round Pushbutton
  R1 = Trimmer Potentiometer [maximum_resistance=10kΩ package=THT]  # not connected

nets:
  3V3: WeMos_D1_Mini1.3V3, DS1.VDD
  5V: WeMos_D1_Mini1.5V, WeMos_D1_Mini2.5V, Part1.VDD, HLK-PM1.+Vo
  N1: WeMos_D1_Mini1.D3, DS1.DQ
  N2: WeMos_D1_Mini1.D4, Part1.DIN
  GND: WeMos_D1_Mini1.G, WeMos_D1_Mini2.G, DS1.GND, Part1.VSS, U1.-, HLK-PM1.-Vo, S1.leg0
  N3: WeMos_D1_Mini2.D2, S1.leg1
  N4: WeMos_D1_Mini2.D4, U1.+
  N5: U1.T1, V1.V+, HLK-PM1.AC#0
  N6: U1.T2, U2.+
  N7: V1.V-, HLK-PM1.AC#1, U2.-
